# Fritzing sketch esquematico-fritzing (saved by Fritzing 0.9.3b)

parts:
  LCD2004-I2C1 = LCD2004-I2C
  WeMos_D1_Mini1 = WeMos D1 Mini
  LCD2004-I2C2 = LCD2004-I2C
  Componente1 = Arduino Uno (Rev3) - ICSP

nets:
  N1: LCD2004-I2C1.GND, WeMos_D1_Mini1.G
  VCC: LCD2004-I2C1.VCC, WeMos_D1_Mini1.5V
  N2: LCD2004-I2C1.SDA, WeMos_D1_Mini1.D2
  N3: LCD2004-I2C1.SCL, WeMos_D1_Mini1.D1
  GND: LCD2004-I2C2.GND, Componente1.GND
  VCC_2: LCD2004-I2C2.VCC, Componente1.5V
  N4: LCD2004-I2C2.SDA, Componente1.A4/SDA
  N5: LCD2004-I2C2.SCL, Componente1.A5/SCL

custom parts:
  LCD2004-I2C: A standard character display with 4x20 characters. Comes in many colors with LCM2004 IIC attached.
